// Logisim project computer.circ as structural Verilog: 1 circuit, main circuit main
module main (
);

  wire dipswitch_3_sw1, dipswitch_3_sw2, dipswitch_3_sw3, dipswitch_3_sw4, dipswitch_5_sw1, dipswitch_5_sw2,
       dipswitch_5_sw3, dipswitch_5_sw4, dipswitch_6_sw1, dipswitch_7_p1, dipswitch_12_sw1,
       multiplexer_1_out, multiplexer_2_out, multiplexer_3_out, multiplexer_4_out, n7447_1_pin3,
       n7447_1_pin9, n7447_1_pin10, n7447_1_pin11, n7447_1_pin12, n7447_1_pin13, n7447_1_pin14,
       n7447_1_pin15, n7486_1_pin3, n7486_1_pin6, n7486_1_pin8, n7486_1_pin11, n74193_1_pin2, n74193_1_pin3,
       n74193_1_pin4, n74193_1_pin5, n74193_1_pin6, n74193_1_pin7, n74193_1_pin14, n74245_2_pin1,
       n74245_2_pin11, n74245_2_pin12, n74245_2_pin13, n74245_2_pin14, n74245_2_pin15, n74245_2_pin16,
       n74245_2_pin17, n74245_2_pin18, n74273_1_pin1, n74273_1_pin2, n74273_1_pin3, n74273_1_pin4,
       n74273_1_pin5, n74273_1_pin6, n74273_1_pin7, n74273_1_pin8, n74273_1_pin9, n74273_1_pin11,
       n74273_1_pin12, n74273_1_pin13, n74273_1_pin14, n74273_1_pin15, n74273_1_pin16, n74273_1_pin17,
       n74273_1_pin18, n74273_1_pin19, n74273_2_pin1, n74273_2_pin2, n74273_2_pin5, n74273_2_pin6,
       n74273_2_pin9, n74273_2_pin11, n74273_2_pin13, n74273_2_pin14, n74273_2_pin17, n74273_2_pin18,
       n74283_1_pin1, n74283_1_pin4, n74283_1_pin10, n74283_1_pin13;

  _74245 u_74245_1 ();  // open: pin1, pin2, pin3, pin4, pin5, pin6, pin7, pin8, pin9, pin19, pin18, pin17, pin16, pin15, pin14, pin13, pin12, pin11
  RAM ram_1 ();  // open: addr, we, oe, clk, din, dout
  DipSwitch dipswitch_1 ();  // open: sw1, sw2, sw3, sw4, sw5, sw6, sw7, sw8
  LED led_1 (.in(n74273_1_pin19));
  _74273 u_74273_1 (
    .pin1(n74273_1_pin1), .pin2(n74273_1_pin2), .pin3(n74273_1_pin3), .pin4(n74273_1_pin4),
    .pin5(n74273_1_pin5), .pin6(n74273_1_pin6), .pin7(n74273_1_pin7), .pin8(n74273_1_pin8),
    .pin9(n74273_1_pin9), .pin19(n74273_1_pin19), .pin18(n74273_1_pin18), .pin17(n74273_1_pin17),
    .pin16(n74273_1_pin16), .pin15(n74273_1_pin15), .pin14(n74273_1_pin14), .pin13(n74273_1_pin13),
    .pin12(n74273_1_pin12), .pin11(n74273_1_pin11));
  LED led_2 (.in(n74273_1_pin2));
  DipSwitch #(.number(1)) dipswitch_2 (.sw1(n74273_1_pin1));
  DipSwitch #(.number(4)) dipswitch_3 (
    .sw1(dipswitch_3_sw1), .sw2(dipswitch_3_sw2), .sw3(dipswitch_3_sw3), .sw4(dipswitch_3_sw4));
  LED led_3 (.in(n74273_1_pin16));
  LED led_4 (.in(n74273_1_pin15));
  LED led_5 (.in(n74273_1_pin5));
  LED led_6 (.in(n74273_1_pin6));
  DipSwitch #(.number(4)) dipswitch_4 (
    .sw1(n74273_1_pin3), .sw2(n74273_1_pin4), .sw3(n74273_1_pin7), .sw4(n74273_1_pin8));
  DipSwitch #(.number(4)) dipswitch_5 (
    .sw1(dipswitch_5_sw1), .sw2(dipswitch_5_sw2), .sw3(dipswitch_5_sw3), .sw4(dipswitch_5_sw4));
  Clock clock_1 (.out(n74273_1_pin11));
  LED led_7 (.in(n74273_1_pin12));
  LED led_8 (.in(n74273_1_pin9));
  DipSwitch #(.number(1)) dipswitch_6 (.sw1(dipswitch_6_sw1));
  // DipSwitch #(.number(1)) dipswitch_7: pin names not known; wires that end beside it: dipswitch_7_p1
  _74245 u_74245_2 (
    .pin1(n74245_2_pin1), .pin2(n74273_1_pin2), .pin3(n74273_1_pin5), .pin4(n74273_1_pin6),
    .pin5(n74273_1_pin9), .pin6(n74273_1_pin13), .pin7(n74273_1_pin14), .pin8(n74273_1_pin17),
    .pin9(n74273_1_pin18), .pin19(dipswitch_7_p1), .pin18(n74245_2_pin18), .pin17(n74245_2_pin17),
    .pin16(n74245_2_pin16), .pin15(n74245_2_pin15), .pin14(n74245_2_pin14), .pin13(n74245_2_pin13),
    .pin12(n74245_2_pin12), .pin11(n74245_2_pin11));
  DipSwitch #(.number(1)) dipswitch_8 (.sw1(n74245_2_pin1));
  _7486 u_7486_1 (
    .pin1(dipswitch_5_sw1), .pin2(dipswitch_6_sw1), .pin3(n7486_1_pin3), .pin4(dipswitch_6_sw1),
    .pin5(dipswitch_5_sw2), .pin6(n7486_1_pin6), .pin13(dipswitch_6_sw1), .pin12(dipswitch_5_sw3),
    .pin11(n7486_1_pin11), .pin10(dipswitch_6_sw1), .pin9(dipswitch_5_sw4), .pin8(n7486_1_pin8));
  _74193 u_74193_1 (
    .pin2(n74193_1_pin2), .pin3(n74193_1_pin3), .pin4(n74193_1_pin4), .pin5(n74193_1_pin5),
    .pin6(n74193_1_pin6), .pin7(n74193_1_pin7), .pin14(n74193_1_pin14), .pin11(n74193_1_pin4));  // open: pin1, pin15, pin13, pin12, pin10, pin9
  Clock clock_2 (.out(n74193_1_pin5));
  _74283 u_74283_1 (
    .pin1(n74283_1_pin1), .pin2(n7486_1_pin6), .pin3(dipswitch_3_sw2), .pin4(n74283_1_pin4),
    .pin5(dipswitch_3_sw1), .pin6(n7486_1_pin3), .pin7(dipswitch_6_sw1), .pin15(n7486_1_pin11),
    .pin14(dipswitch_3_sw3), .pin13(n74283_1_pin13), .pin12(dipswitch_3_sw4), .pin11(n7486_1_pin8),
    .pin10(n74283_1_pin10));  // open: pin9
  _74273 u_74273_2 (
    .pin1(n74273_2_pin1), .pin2(n74273_2_pin2), .pin3(n74245_2_pin18), .pin4(n74245_2_pin17),
    .pin5(n74273_2_pin5), .pin6(n74273_2_pin6), .pin7(n74245_2_pin16), .pin8(n74245_2_pin15),
    .pin9(n74273_2_pin9), .pin19(n74245_2_pin11), .pin18(n74273_2_pin18), .pin17(n74273_2_pin17),
    .pin16(n74245_2_pin12), .pin15(n74245_2_pin13), .pin14(n74273_2_pin14), .pin13(n74273_2_pin13),
    .pin12(n74245_2_pin14), .pin11(n74273_2_pin11));
  DipSwitch #(.number(1)) dipswitch_9 (.sw1(n74273_2_pin1));
  LED led_9 (.in(n74245_2_pin11));
  LED led_10 (.in(n74245_2_pin12));
  LED led_11 (.in(n74273_2_pin5));
  LED led_12 (.in(n74273_2_pin2));
  DipSwitch #(.number(1)) dipswitch_10 (.sw1(n74193_1_pin14));
  // DipSwitch #(.number(4)) dipswitch_11: pin names not known; wires that end beside it: n74273_2_pin18, n74273_2_pin17, n74273_2_pin14, n74273_2_pin13
  LED led_13 (.in(n74245_2_pin13));
  LED led_14 (.in(n74245_2_pin14));
  LED led_15 (.in(n74273_2_pin6));
  LED led_16 (.in(n74273_2_pin9));
  LED led_17 (.in(n74193_1_pin3));
  LED led_18 (.in(n74193_1_pin2));
  LED led_19 (.in(n74193_1_pin6));
  LED led_20 (.in(n74283_1_pin13));
  LED led_21 (.in(n74283_1_pin4));
  LED led_22 (.in(n74283_1_pin1));
  Clock clock_3 (.out(n74273_2_pin11));
  LED led_23 (.in(n74193_1_pin7));
  LED led_24 (.in(n74283_1_pin10));
  Multiplexer multiplexer_1 (.in0(n74193_1_pin3), .in1(n74283_1_pin4), .out(multiplexer_1_out), .sel(dipswitch_12_sw1));
  Multiplexer multiplexer_2 (.in0(n74193_1_pin2), .in1(n74283_1_pin1), .out(multiplexer_2_out), .sel(dipswitch_12_sw1));
  Multiplexer multiplexer_3 (
    .in0(n74193_1_pin6), .in1(n74283_1_pin13), .out(multiplexer_3_out), .sel(dipswitch_12_sw1));
  Multiplexer multiplexer_4 (
    .in0(n74193_1_pin7), .in1(n74283_1_pin10), .out(multiplexer_4_out), .sel(dipswitch_12_sw1));
  DipSwitch #(.number(1)) dipswitch_12 (.sw1(dipswitch_12_sw1));
  _7447 u_7447_1 (
    .pin1(multiplexer_2_out), .pin2(multiplexer_3_out), .pin3(n7447_1_pin3), .pin4(n7447_1_pin3),
    .pin5(n7447_1_pin3), .pin6(multiplexer_4_out), .pin7(multiplexer_1_out), .pin15(n7447_1_pin15),
    .pin14(n7447_1_pin14), .pin13(n7447_1_pin13), .pin12(n7447_1_pin12), .pin11(n7447_1_pin11),
    .pin10(n7447_1_pin10), .pin9(n7447_1_pin9));
  ROM rom_1 ();  // open: addr, data
  _7_Segment_Display #(.active("false"), .decimalPoint("false")) u_7_segment_display_1 (
    .g(n7447_1_pin14), .f(n7447_1_pin15), .a(n7447_1_pin13), .b(n7447_1_pin12), .e(n7447_1_pin9),
    .d(n7447_1_pin10), .c(n7447_1_pin11));
  // also tied to VCC on the sheet: {n74193_1_pin4, n7447_1_pin3}

  // Notes on the sheet:
  //   Common-Anode
endmodule
